# Fritzing sketch esquema (saved by Fritzing 0.9.2b)
stripboards: 1

parts:
  Parte1 = Arduino Nano (Rev3.0)
  Q1 = TIP120 Hi-Current Darlington Transistor
  Q2 = TIP120 Hi-Current Darlington Transistor
  Q3 = TIP120 Hi-Current Darlington Transistor
  LPD8806_RGB_LED_Strip1 = LPD8806 RGB LED Strip
  J1 = COMPUTER-PERIPHERAL-POWER [package=computer-peripheral-power]
  S1 = Round Pushbutton
  R1 = Resistor [tolerance=±5% resistance=10k package=THT]

nets:
  N1: Parte1.D3, Q3.BASE
  N2: Parte1.D4, Q2.BASE
  N3: Parte1.D5, Q1.BASE
  GND: Parte1.GND, Q1.EMITTER, Q2.EMITTER, Q3.EMITTER, J1.GND, J1.NC, R1.Pin_1
  N4: Q1.COLLECTOR, LPD8806_RGB_LED_Strip1.+12V
  N5: Q2.COLLECTOR, LPD8806_RGB_LED_Strip1.R
  N6: Q3.COLLECTOR, LPD8806_RGB_LED_Strip1.G
  N7: S1.leg0, R1.Pin_0

custom parts:
  LPD8806 RGB LED Strip: Digitally addressable RGB LED strip

// code stored in the sketch: Tira-de-led-Arduino.ino
/**
   @file Tira-de-led-Arduino.ino
   @brief Gestion de una tira de led
   @author Pablo Rocamora pablojoserocamora@gmail.com
   @date 14/12/2016
*/

//Info: http://www.prometec.net/tira-de-leds/

#define DEBUG true

#define LED_R 3      //ROJO
#define LED_G 4      //VERDE
#define LED_B 5      //AZUL
#define BUTTON 6     //Conexion del boton

//inicio contador en 1 para que en la primera pulsacion entre en el rojo
int contador = 1;
boolean lastButton = LOW;   //contiene el estado anterioR del boton
boolean currentButton = LOW;  //Contiene el estado actual del boton

void setup() {
  pinMode (LED_R, OUTPUT);
  pinMode (LED_G, OUTPUT);
  pinMode (LED_B, OUTPUT);
  pinMode(BUTTON, INPUT_PULLUP);   // Para leel el boton
  pinMode(13, OUTPUT);         // Para usar un LED de encendido
  if (DEBUG) {
    Serial.begin(115200);
    Serial.println("inicio");
  }
}


/*
  Debouncing Function
  Pass it the previous button state,
  and get back the current debounced button state.
*/
boolean debounce(boolean last) {
  boolean current = digitalRead(BUTTON);    //Read the button state
  if (last != current) {            //if it's different?
    delay(5);               //wait 5ms
    current = digitalRead(BUTTON);      //read it again
  }
  return current;               //return the current value
}


void loop() {
  currentButton = debounce(lastButton);       //read debounced state
  if (lastButton == LOW && currentButton == HIGH) {  //if it was pressed?
    if (DEBUG)
      Serial.println("CONTADOR: " + String(contador));
    //delay(500);

    switch (contador) {
      case 0:
        if (DEBUG)
          Serial.println("APAGAR");
        contador++;
        digitalWrite(LED_R, LOW);
        digitalWrite(LED_G, LOW);
        digitalWrite(LED_B, LOW);
        break;

      case 1: //ROJO
        if (DEBUG)
          Serial.println("rojo");
        contador++;
        digitalWrite(LED_R, HIGH);
        digitalWrite(LED_G, LOW);
        digitalWrite(LED_B, LOW);
        break;

      case 2: //VERDE
        if (DEBUG)
          Serial.println("verde");
        contador++;
        digitalWrite(LED_R, LOW);
        digitalWrite(LED_G, HIGH);
        digitalWrite(LED_B, LOW);
        break;

      case 3: //AZUL
        if (DEBUG)
          Serial.println("azul");
        contador = 0;
        digitalWrite(LED_R, LOW);
        digitalWrite(LED_G, LOW);
        digitalWrite(LED_B, HIGH);
        break;

      default:  //nunca debria llegar aqui
        contador = 0;
        if (DEBUG) {
          Serial.println("HAY ALGUN FALLO CON EL CONTADOR");
          Serial.println(contador);
        }
        break;
    }
  }

  lastButton = currentButton;
}
