# Fritzing sketch esquema_compacto (saved by Fritzing 0.9.2b)
perfboards: 1

parts:
  LPD8806_RGB_LED_Strip1 = LPD8806 RGB LED Strip
  Q4 = TIP120 Hi-Current Darlington Transistor
  Q5 = TIP120 Hi-Current Darlington Transistor
  Q6 = TIP120 Hi-Current Darlington Transistor
  J4 = COMPUTER-PERIPHERAL-POWER [package=computer-peripheral-power]
  JP1 = Header 1 [package=1x01_offset]
  JP2 = Header 1 [package=1x01_offset]
  JP7 = Header 4 [package=molex-1x4_lock]
  JP8 = Header 4 [package=molex-1x4_lock]
  Parte1 = Arduino Nano (Rev3.0)

nets:
  N1: LPD8806_RGB_LED_Strip1.+12V, Q4.COLLECTOR
  N2: LPD8806_RGB_LED_Strip1.G, Q6.COLLECTOR
  N3: LPD8806_RGB_LED_Strip1.R, Q5.COLLECTOR
  N4: LPD8806_RGB_LED_Strip1.B, J4.5V
  N5: Q4.EMITTER, Q6.EMITTER
  N6: Q5.BASE, Parte1.D3
  N7: Q6.BASE, Parte1.D2
  N8: J4.12V, JP1.1
  GND: J4.GND, J4.NC, JP2.1, Parte1.GND
  N9: JP7.1, JP8.4, Parte1.D8
  N10: JP7.2, Parte1.D7
  N11: JP8.1, Parte1.D5
  N12: JP8.2, Parte1.D6
  N13: JP8.3, Parte1.D9

custom parts:
  LPD8806 RGB LED Strip: Digitally addressable RGB LED strip

// code stored in the sketch: Tira-de-led-Arduino.ino
/**
   @file Tira-de-led-Arduino.ino
   @brief Gestion de una tira de led
   @author Pablo Rocamora pablojoserocamora@gmail.com
   @date 14/12/2016
*/

//Info: http://www.prometec.net/tira-de-leds/

#define DEBUG true

#define LED_R 2      //ROJO
#define LED_G 3      //VERDE
#define LED_B 4      //AZUL

#define INPUT_D 6     //APAGAR
#define INPUT_A 7     //ROJO
#define INPUT_B 8     //VERDE
#define INPUT_C 9     //AZUL

#define LECTURA 5     //

//inicio contador en 1 para que en la primera pulsacion entre en el rojo
boolean currentButton = false;  //Contiene el estado actual del boton

unsigned long TIEMPO_ACTUAL = 0; //last time messages' scan has been done
#define TIEMPO_ESPERA 100 // mean time between scan messages

void setup() {
  pinMode(LED_R, OUTPUT);
  pinMode(LED_G, OUTPUT);
  pinMode(LED_B, OUTPUT);
  pinMode(INPUT_A, INPUT);
  pinMode(INPUT_B, INPUT);   // Para leel el boton
  pinMode(INPUT_C, INPUT);
  pinMode(INPUT_D, INPUT);
  pinMode(LECTURA, INPUT);

  if (DEBUG) {
    Serial.begin(115200);
    Serial.println("inicio");
  }
}

String checkBoolean(bool valor) {
  if (String(valor) == "1")
    return "True";
  return "False";
}

void loop() {
  if (millis() > TIEMPO_ACTUAL + TIEMPO_ESPERA) {
    TIEMPO_ACTUAL = millis();

    if (digitalRead(LECTURA)) {    // Si hay dato valido
      //if (DEBUG)
      // Serial.println("currentButton: " + checkBoolean(currentButton));

      if (digitalRead(INPUT_A)) {
        bool estado = digitalRead(LED_R);
        if (DEBUG)
          Serial.println("rojo: " + checkBoolean(!estado));
        digitalWrite(LED_R, !estado);
      }

      if (digitalRead(INPUT_B)) {
        bool estado = digitalRead(LED_G);
        if (DEBUG)
          Serial.println("verde: " + checkBoolean(!estado));
        digitalWrite(LED_G,  !estado);
      }

      if (digitalRead(INPUT_C)) {
        bool estado = digitalRead(LED_B);
        if (DEBUG)
          Serial.println("azul: " + checkBoolean(!estado));
        digitalWrite(LED_B,  !estado);
      }

      if (digitalRead(INPUT_D)) {
        if (DEBUG)
          Serial.println("APAGAR");
        digitalWrite(LED_R,  LOW);
        digitalWrite(LED_G,  LOW);
        digitalWrite(LED_B,  LOW);
      }

      if (DEBUG) {
        Serial.println();
        Serial.println("rojo: " + checkBoolean(digitalRead(LED_R)));
        Serial.println("verde: " + checkBoolean(digitalRead(LED_G)));
        Serial.println("azul: " + checkBoolean(digitalRead(LED_B)));
        Serial.println();
        Serial.println();
        Serial.println();
      }
      delay(300);
    }
  }
}
